// Logisim project task_2.6.circ as structural Verilog: 3 circuits, main circuit CPU_main
module CPU_main (
);

  wire and_1_out, clock_1_out, instruction_decoding_unit_1_branch_unc, instruction_decoding_unit_1_stop,
       instruction_decoding_unit_1_use_memory, instruction_decoding_unit_1_write_acc,
       instruction_decoding_unit_1_write_memory, not_1_out;
  wire [3:0] instruction_decoding_unit_1_alu_operation;
  wire [7:0] ACC_q, adder_1_out, alu_1_alu_to_acc, Data_Memory_dout, instruction_decoding_unit_1_addr_or_imm,
       multiplexer_1_out, multiplexer_2_out, multiplexer_3_out, PC_q;
  wire [15:0] Instruction_Memory_data;

  Multiplexer #(.width(8)) multiplexer_1 (
    .in0(adder_1_out), .in1(instruction_decoding_unit_1_addr_or_imm), .out(multiplexer_1_out),
    .sel(instruction_decoding_unit_1_branch_unc));
  Register PC (.D(multiplexer_1_out), .clk(and_1_out), .Q(PC_q));  // open: en, clr
  Clock clock_1 (.out(clock_1_out));
  Adder adder_1 (.a(PC_q), .b(8'h1), .out(adder_1_out));  // open: cin, cout
  ROM #(.dataWidth(16)) Instruction_Memory (.addr(PC_q), .data(Instruction_Memory_data));
  Instruction_Decoding_Unit instruction_decoding_unit_1 (
    .Instruction(Instruction_Memory_data), .ALU_Operation(instruction_decoding_unit_1_alu_operation),
    .Write_ACC(instruction_decoding_unit_1_write_acc),
    .Write_Memory(instruction_decoding_unit_1_write_memory),
    .Use_Memory(instruction_decoding_unit_1_use_memory), .Branch_unc(instruction_decoding_unit_1_branch_unc),
    .Stop(instruction_decoding_unit_1_stop), .Addr_or_Imm(instruction_decoding_unit_1_addr_or_imm));  // open: BNEZ
  not not_1 (not_1_out, instruction_decoding_unit_1_stop);
  and and_1 (and_1_out, not_1_out, clock_1_out);
  RAM #(.asyncread("true"), .clearpin("true")) Data_Memory (
    .addr(multiplexer_2_out), .we(instruction_decoding_unit_1_write_memory), .clk(and_1_out), .din(ACC_q),
    .dout(Data_Memory_dout));  // open: oe, clr
  Multiplexer #(.width(8)) multiplexer_2 (
    .in0({8{1'b0}}), .in1(instruction_decoding_unit_1_addr_or_imm), .out(multiplexer_2_out),
    .sel(instruction_decoding_unit_1_use_memory));
  Multiplexer #(.width(8)) multiplexer_3 (
    .in0(instruction_decoding_unit_1_addr_or_imm), .in1(Data_Memory_dout), .out(multiplexer_3_out),
    .sel(instruction_decoding_unit_1_use_memory));
  Register ACC (
    .D(alu_1_alu_to_acc), .en(instruction_decoding_unit_1_write_acc), .clk(and_1_out), .Q(ACC_q));  // open: clr
  ALU alu_1 (
    .From_ACC(ACC_q), .Input2(multiplexer_3_out), .ALU_Operation(instruction_decoding_unit_1_alu_operation),
    .ALU_to_ACC(alu_1_alu_to_acc));  // open: ACC_NE_Zero

  // Notes on the sheet:
  //   contents of Instruction_Memory (hex, n*v repeats v):
  //   1003 3000 1100 3001 1100 3002 1101 3003 4006
  //   Student id: 23643001
endmodule

module Instruction_Decoding_Unit (
  input  [15:0] Instruction,
  output [3:0] ALU_Operation,
  output Write_ACC,
  output Write_Memory,
  output Use_Memory,
  output Branch_unc,
  output BNEZ,
  output Stop,
  output [7:0] Addr_or_Imm
);

  wire decoder_1_out1, decoder_1_out2;

  Decoder #(.select(4)) decoder_1 (
    .out1(decoder_1_out1), .out2(decoder_1_out2), .out3(Write_Memory), .out4(Branch_unc), .out5(BNEZ),
    .out15(Stop), .sel(Instruction[15:12]));  // open: out0, out6, out7, out8, out9, out10, out11, out12, out13, out14, en
  or or_1 (Write_ACC, decoder_1_out1, decoder_1_out2);
  or or_2 (Use_Memory, decoder_1_out2, Write_Memory);

  assign Addr_or_Imm = Instruction[7:0];
  assign ALU_Operation = Instruction[11:8];
endmodule

module ALU (
  input  [7:0] From_ACC,
  input  [7:0] Input2,
  input  [3:0] ALU_Operation,
  output ACC_NE_Zero,
  output [7:0] ALU_to_ACC
);

  wire [7:0] adder_1_out, and_1_out, or_1_out, subtractor_1_out;

  Adder adder_1 (.a(From_ACC), .b(Input2), .out(adder_1_out));  // open: cin, cout
  assign and_1_out = From_ACC & Input2;  // AND_Gate and_1, 8 bits wide
  Subtractor subtractor_1 (.a(From_ACC), .b(Input2), .out(subtractor_1_out));  // open: bin, bout
  assign or_1_out = From_ACC | Input2;  // OR_Gate or_1, 8 bits wide
  Multiplexer #(.select(4), .width(8)) multiplexer_1 (
    .in0(Input2), .in1(adder_1_out), .in2(or_1_out), .in3(and_1_out), .in4(subtractor_1_out),
    .out(ALU_to_ACC), .sel(ALU_Operation));  // open: in5, in6, in7, in8, in9, in10, in11, in12, in13, in14, in15
endmodule
