// Logisim project rom_memory.circ as structural Verilog: 2 circuits, main circuit main
module main (
);

  wire clock_1_out;
  wire [7:0] adder_1_out, adder_2_out, register_1_q, register_2_q, rom_1_data;

  Clock clock_1 (.out(clock_1_out));
  Register register_1 (.D(adder_1_out), .clk(clock_1_out), .Q(register_1_q));  // open: en, clr
  Adder adder_1 (.a(register_1_q), .b(8'h1), .out(adder_1_out));  // open: cin, cout
  ROM rom_1 (.addr(register_1_q), .data(rom_1_data));
  Adder adder_2 (.a(register_2_q), .b(rom_1_data), .out(adder_2_out));  // open: cin, cout
  Register register_2 (.D(adder_2_out), .clk(clock_1_out), .Q(register_2_q));  // open: en, clr

  // Notes on the sheet:
  //   contents of rom_1 (hex, n*v repeats v):
  //   1 3 5 7 9 b d f 2 4 5 1 8 1d 1e 1 1 5 7 e 1d 1f 9 2 5 7 f a e 6 5 4 0 1 0 1 0 2 0 e 0 5 6 0 0 f 1a
  //   1a
endmodule

module sub (
);

  wire clock_1_out;
  wire [15:0] adder_1_out, adder_3_out, register_1_q, register_2_q, rom_1_data;

  Clock clock_1 (.out(clock_1_out));
  Register #(.width(16)) register_1 (.D(adder_1_out), .clk(clock_1_out), .Q(register_1_q));  // open: en, clr
  Adder #(.width(16)) adder_1 (.a(register_1_q), .b(16'h1), .out(adder_1_out));  // open: cin, cout
  Adder adder_2 ();  // open: a, b, out, cin, cout
  Subtractor subtractor_1 ();  // open: a, b, out, bin, bout
  // AND_Gate and_1 is placed but not wired
  ROM #(.addrWidth(16), .dataWidth(16)) rom_1 (.addr(register_1_q), .data(rom_1_data));
  Adder #(.width(16)) adder_3 (.a(register_2_q), .b(rom_1_data), .out(adder_3_out));  // open: cin, cout
  Register #(.width(16)) register_2 (.D(adder_3_out), .clk(clock_1_out), .Q(register_2_q));  // open: en, clr

  // Notes on the sheet:
  //   contents of rom_1 (hex, n*v repeats v):
  //   1 3 5 7 9 b d f 2 4 5 1 8 1d 1e 1 1 5 7 e 1d 1f 9 2 5 7 f a e 6 5 4 0 1 0 1 0 2 0 e 0 5 6 0 0 f 1a
  //   1a
endmodule
