// Logisim project logic_gate_a_W1.circ as structural Verilog: 1 circuit, main circuit main
module main (
  input  A1,
  input  B1,
  input  A2,
  input  B2,
  input  A3,
  input  B3,
  input  A,
  input  B,
  input  C,
  input  in_10,
  input  in_11,
  input  C1,
  input  in_13,
  input  in_14,
  input  in_15,
  input  in_16,
  input  in_17,
  input  in_18,
  output X1,
  output X2,
  output X3,
  output X,
  output out_23,
  output out_24,
  output out_25
);

  wire and_1_out, nand_1_out, nand_2_out, nand_3_out, or_1_out;

  or or_1 (or_1_out, in_17, in_18);
  nand nand_1 (nand_1_out, A1, B1);
  nand nand_2 (nand_2_out, A, B);
  nand nand_3 (nand_3_out, in_11, C1);
  and and_1 (and_1_out, in_13, in_14);
  not not_1 (X1, nand_1_out);
  nor nor_1 (X2, A2, B2);
  xor xor_1 (X3, A3, B3);
  or or_2 (out_24, and_1_out, in_15);
  and and_2 (out_25, in_16, or_1_out);
  nand nand_4 (X, nand_2_out, C);
  nand nand_5 (out_23, in_10, nand_3_out);
endmodule
