// Logisim project logic_gate_b_W1.circ as structural Verilog: 1 circuit, main circuit main
module main (
  input  L,
  input  M,
  input  P,
  input  J,
  input  in_5,
  input  K,
  output C,
  output X
);

  wire and_1_out, not_1_out, or_1_out;

  or or_1 (or_1_out, M, P);
  and and_1 (and_1_out, J, in_5);
  not not_1 (not_1_out, K);
  and and_2 (C, L, or_1_out);
  and and_3 (X, and_1_out, not_1_out);
endmodule
