// Logisim project w2_labA.circ as structural Verilog: 2 circuits, main circuit half_adder
module half_adder (
  input  A,
  input  B,
  output carry,
  output sum
);

  and and_1 (carry, A, B);
  xor xor_1 (sum, A, B);
endmodule

module full_adder (
  input  in_1,
  input  in_2,
  input  in_3,
  output carry,
  output sum
);

  wire half_adder_1_carry, half_adder_1_sum, half_adder_2_carry;

  half_adder half_adder_1 (.A(in_1), .B(in_2), .carry(half_adder_1_carry), .sum(half_adder_1_sum));
  half_adder half_adder_2 (.A(half_adder_1_sum), .B(in_3), .carry(half_adder_2_carry), .sum(sum));
  or or_1 (carry, half_adder_1_carry, half_adder_2_carry);
endmodule
