// Logisim project w2_labB.circ as structural Verilog: 1 circuit, main circuit main
module main (
  input  [7:0] in_1,
  input  [7:0] in_2,
  input  [7:0] in_3,
  input  [7:0] in_4,
  output [7:0] out_5,
  output [7:0] out_6
);

  wire [7:0] adder_1_out, adder_2_out, adder_3_out;

  Adder adder_1 (.a(in_3), .b(in_4), .out(adder_1_out));  // open: cin, cout
  Adder adder_2 (.a(in_1), .b(8'ha), .out(adder_2_out));  // open: cin, cout
  Adder adder_3 (.a(in_2), .b(adder_1_out), .out(adder_3_out));  // open: cin, cout
  assign out_5 = in_1 | adder_2_out;  // OR_Gate or_1, 8 bits wide
  assign out_6 = adder_3_out | adder_3_out;  // OR_Gate or_2, 8 bits wide
endmodule
