// Logisim project logicw3lab.circ as structural Verilog: 1 circuit, main circuit main
module main (
  input  [2:0] C0,
  input  [2:0] C1,
  input  [2:0] C2,
  input  [2:0] C3,
  input  SEL
);

  Multiplexer multiplexer_1 ();  // open: in0, in1, out, sel
endmodule
