// Logisim project alu_w4.circ as structural Verilog: 1 circuit, main circuit main
module main (
  input  [7:0] A,
  input  [7:0] B,
  input  [1:0] ALU_Opcode,
  output [7:0] ALU_Out
);

  wire [7:0] adder_1_out, and_1_out, subtractor_1_out;

  Subtractor subtractor_1 (.a(A), .b(8'h1), .out(subtractor_1_out));  // open: bin, bout
  Adder adder_1 (.a(A), .b(B), .out(adder_1_out));  // open: cin, cout
  assign and_1_out = A & B;  // AND_Gate and_1, 8 bits wide
  Multiplexer #(.select(2), .width(8)) multiplexer_1 (
    .in0(subtractor_1_out), .in1(adder_1_out), .in2(and_1_out), .out(ALU_Out), .sel(ALU_Opcode));  // open: in3
endmodule
