// Logisim project traffic.circ as structural Verilog: 1 circuit, main circuit main
module main (
  input  [1:0] in_1
);

  wire decoder_1_out0, decoder_1_out1, decoder_1_out2, decoder_1_out3, or_1_out, or_2_out;

  Decoder #(.select(2)) decoder_1 (
    .out0(decoder_1_out0), .out1(decoder_1_out1), .out2(decoder_1_out2), .out3(decoder_1_out3), .sel(in_1));  // open: en
  or or_1 (or_1_out, decoder_1_out0, decoder_1_out1);
  LED led_1 (.in(or_1_out));
  or or_2 (or_2_out, decoder_1_out1, decoder_1_out3);
  LED led_2 (.in(decoder_1_out2));
  LED led_3 (.in(or_2_out));
endmodule
