// Logisim project W5_automated_traffic_register.circ as structural Verilog: 1 circuit, main circuit main
module main (
);

  wire clock_1_out, decoder_1_out0, decoder_1_out1, decoder_1_out2, decoder_1_out3, or_1_out, or_2_out;
  wire [1:0] adder_1_out, register_1_q;

  Decoder #(.select(2)) decoder_1 (
    .out0(decoder_1_out0), .out1(decoder_1_out1), .out2(decoder_1_out2), .out3(decoder_1_out3),
    .sel(register_1_q));  // open: en
  or or_1 (or_1_out, decoder_1_out0, decoder_1_out1);
  Adder #(.width(2)) adder_1 (.a(register_1_q), .b(2'b01), .out(adder_1_out));  // open: cin, cout
  Clock clock_1 (.out(clock_1_out));
  LED led_1 (.in(or_1_out));
  or or_2 (or_2_out, decoder_1_out1, decoder_1_out3);
  LED led_2 (.in(decoder_1_out2));
  Register #(.width(2)) register_1 (.D(adder_1_out), .clk(clock_1_out), .Q(register_1_q));  // open: en, clr
  LED led_3 (.in(or_2_out));
endmodule
