// Logisim project W5_lab_A.circ as structural Verilog: 3 circuits, main circuit main
module main (
  input  inv_set,
  input  inv_reset,
  output q,
  output not_q
);

  nand s (q, inv_set, not_q);
  nand r (not_q, q, inv_reset);
endmodule

module sub (
);

  wire main_1_not_q, main_1_q, not_1_out, not_2_out, R_out, s_out;

  Button s (.out(s_out));
  Button R (.out(R_out));
  not not_1 (not_1_out, s_out);
  not not_2 (not_2_out, R_out);
  main main_1 (.inv_set(not_1_out), .inv_reset(not_2_out), .q(main_1_q), .not_q(main_1_not_q));
  LED led_1 (.in(main_1_q));
  LED led_2 (.in(main_1_not_q));
endmodule

module FLIP_FLOP (
  input  in_1
);

  wire main_1_not_q, main_2_not_q, main_2_q;

  // AND_Gate and_1 has open pins: in1=main_1_not_q, out=open
  main main_1 (.inv_set(main_2_not_q), .not_q(main_1_not_q));  // open: inv_reset, q
  main main_2 (.inv_reset(in_1), .q(main_2_q), .not_q(main_2_not_q));  // open: inv_set
  main main_3 (.inv_set(main_1_not_q), .inv_reset(main_2_q));  // open: q, not_q
endmodule
